// Logisim project first_drafts.circ as structural Verilog
module Y2_0 (
  input  A7,
  input  A6,
  input  A5,
  input  A4,
  input  A3,
  input  A2,
  input  A1,
  input  A0,
  output Y2,
  output Y1,
  output Y0,
  output NONE
);

  wire and_1_out, and_2_out, and_3_out, and_4_out, and_5_out, not_1_out, not_2_out, not_3_out, not_4_out,
       not_5_out, not_6_out, not_7_out, not_8_out;

  not not_1 (not_1_out, A7);
  not not_2 (not_2_out, A6);
  not not_3 (not_3_out, A5);
  not not_4 (not_4_out, A4);
  not not_5 (not_5_out, A3);
  not not_6 (not_6_out, A2);
  not not_7 (not_7_out, A1);
  not not_8 (not_8_out, A0);
  and and_1 (and_1_out, not_3_out, not_4_out, A3);
  and and_2 (and_2_out, not_3_out, not_4_out, A2);
  and and_3 (and_3_out, not_2_out, A5);
  and and_4 (and_4_out, not_2_out, not_4_out, A3);
  and and_5 (and_5_out, not_2_out, not_4_out, not_6_out, A1);
  or or_1 (Y2, A7, A6, A5, A4);
  or or_2 (Y1, A7, A6, and_1_out, and_2_out);
  or or_3 (Y0, A7, and_3_out, and_4_out, and_5_out);
  and and_6 (NONE, not_1_out, not_2_out, not_3_out, not_4_out, not_5_out, not_6_out, not_7_out, not_8_out);
endmodule

module Z2_0 (
  input  A7,
  input  A6,
  input  A5,
  input  A4,
  input  A3,
  input  A2,
  input  A1,
  input  A0,
  output Z2,
  output Z1,
  output Z0
);

  wire and_1_out, and_2_out, and_3_out, and_4_out, and_5_out, and_6_out, not_1_out, not_2_out, not_3_out,
       not_4_out, not_5_out, not_6_out, not_7_out, not_8_out, or_1_out, or_2_out, or_3_out, or_4_out,
       or_5_out;

  not not_1 (not_1_out, A7);
  not not_2 (not_2_out, A6);
  not not_3 (not_3_out, A5);
  not not_4 (not_4_out, A4);
  not not_5 (not_5_out, A3);
  not not_6 (not_6_out, A2);
  not not_7 (not_7_out, A1);
  not not_8 (not_8_out, A0);
  or or_1 (or_1_out, A7, A6);
  or or_2 (or_2_out, or_1_out, A5);
  and and_1 (and_1_out, A5, or_1_out);
  and and_2 (and_2_out, or_2_out, A4);
  and and_3 (and_3_out, A7, A6);
  or or_3 (or_3_out, or_2_out, A4);
  or or_4 (or_4_out, or_3_out, A3);
  and and_4 (and_4_out, A3, or_3_out);
  and and_5 (and_5_out, or_4_out, A2);
  or or_5 (or_5_out, or_4_out, A2);
  or or_6 (Z2, and_1_out, and_2_out, and_3_out);
  or or_7 (Z1, and_3_out, and_4_out, and_5_out);
  and and_6 (and_6_out, or_5_out, A1);
  or or_8 (Z0, and_1_out, and_4_out, and_6_out);
endmodule

module _2_37_sim (
  input  [7:0] in_1,
  output out_2,
  output out_3,
  output out_4,
  output No_input,
  output out_6,
  output out_7,
  output out_8
);

  Y2_0 y2_0_1 (
    .A7(in_1[7]), .A6(in_1[6]), .A5(in_1[5]), .A4(in_1[4]), .A3(in_1[3]), .A2(in_1[2]), .A1(in_1[1]),
    .A0(in_1[0]), .Y2(out_2), .Y1(out_3), .Y0(out_4), .NONE(No_input));
  Z2_0 z2_0_1 (
    .A7(in_1[7]), .A6(in_1[6]), .A5(in_1[5]), .A4(in_1[4]), .A3(in_1[3]), .A2(in_1[2]), .A1(in_1[1]),
    .A0(in_1[0]), .Z2(out_6), .Z1(out_7), .Z0(out_8));
endmodule

// NE
module _32_bit_NE (
  input  [31:0] in_1,
  input  [31:0] in_2,
  output out_3
);

  wire and_1_out, n8_bit_eq_1_out_3, n8_bit_eq_2_out_3, n8_bit_eq_3_out_3, n8_bit_eq_4_out_3;

  _8_bit_EQ u_8_bit_eq_1 (.in_1(in_1[7:0]), .in_2(in_2[7:0]), .out_3(n8_bit_eq_1_out_3));
  _8_bit_EQ u_8_bit_eq_2 (.in_1(in_1[15:8]), .in_2(in_2[15:8]), .out_3(n8_bit_eq_2_out_3));
  _8_bit_EQ u_8_bit_eq_3 (.in_1(in_1[23:16]), .in_2(in_2[23:16]), .out_3(n8_bit_eq_3_out_3));
  _8_bit_EQ u_8_bit_eq_4 (.in_1(in_1[31:24]), .in_2(in_2[31:24]), .out_3(n8_bit_eq_4_out_3));
  not not_1 (out_3, and_1_out);
  and and_1 (and_1_out, n8_bit_eq_1_out_3, n8_bit_eq_2_out_3, n8_bit_eq_3_out_3, n8_bit_eq_4_out_3);
endmodule

module _1_bit_EQ (
  input  in_1,
  input  in_2,
  output out_3
);

  wire and_1_out, and_2_out;

  and and_1 (and_1_out, ~in_1, ~in_2);  // AND_Gate
  and and_2 (and_2_out, in_2, in_1);
  or or_1 (out_3, and_1_out, and_2_out);
endmodule

module _8_bit_EQ (
  input  [7:0] in_1,
  input  [7:0] in_2,
  output out_3
);

  wire n1_bit_eq_1_out_3, n1_bit_eq_2_out_3, n1_bit_eq_3_out_3, n1_bit_eq_4_out_3, n1_bit_eq_5_out_3,
       n1_bit_eq_6_out_3, n1_bit_eq_7_out_3, n1_bit_eq_8_out_3;

  _1_bit_EQ u_1_bit_eq_1 (.in_1(in_2[0]), .in_2(in_1[0]), .out_3(n1_bit_eq_1_out_3));
  _1_bit_EQ u_1_bit_eq_2 (.in_1(in_2[1]), .in_2(in_1[1]), .out_3(n1_bit_eq_2_out_3));
  _1_bit_EQ u_1_bit_eq_3 (.in_1(in_2[2]), .in_2(in_1[2]), .out_3(n1_bit_eq_3_out_3));
  _1_bit_EQ u_1_bit_eq_4 (.in_1(in_2[3]), .in_2(in_1[3]), .out_3(n1_bit_eq_4_out_3));
  _1_bit_EQ u_1_bit_eq_5 (.in_1(in_2[4]), .in_2(in_1[4]), .out_3(n1_bit_eq_5_out_3));
  _1_bit_EQ u_1_bit_eq_6 (.in_1(in_2[5]), .in_2(in_1[5]), .out_3(n1_bit_eq_6_out_3));
  _1_bit_EQ u_1_bit_eq_7 (.in_1(in_2[6]), .in_2(in_1[6]), .out_3(n1_bit_eq_7_out_3));
  _1_bit_EQ u_1_bit_eq_8 (.in_1(in_2[7]), .in_2(in_1[7]), .out_3(n1_bit_eq_8_out_3));
  and and_1 (out_3, n1_bit_eq_1_out_3, n1_bit_eq_2_out_3, n1_bit_eq_3_out_3, n1_bit_eq_4_out_3, n1_bit_eq_5_out_3, n1_bit_eq_6_out_3, n1_bit_eq_7_out_3, n1_bit_eq_8_out_3);
endmodule

module _8_bit_GT (
  input  [7:0] Input_1,
  input  [7:0] Input_2,
  output out_3
);

  wire and_1_out, n4_bit_eq_1_out_3, n4_bit_gt_1_out_3, n4_bit_gt_2_out_3;

  // Probe on Input_1
  // Probe on Input_2
  _4_bit_GT u_4_bit_gt_1 (.in_1(Input_1[3:0]), .in_2(Input_2[3:0]), .out_3(n4_bit_gt_1_out_3));
  _4_bit_GT u_4_bit_gt_2 (.in_1(Input_1[7:4]), .in_2(Input_2[7:4]), .out_3(n4_bit_gt_2_out_3));
  _4_bit_EQ u_4_bit_eq_1 (.in_1(Input_1[7:4]), .in_2(Input_2[7:4]), .out_3(n4_bit_eq_1_out_3));
  and and_1 (and_1_out, n4_bit_gt_1_out_3, n4_bit_eq_1_out_3);
  or or_1 (out_3, and_1_out, n4_bit_gt_2_out_3);
endmodule

module _32_bit_GE (
  input  [31:0] Input_1,
  input  [31:0] Input_2,
  output out_3
);

  wire and_1_out, EQ_out, GT_out, n8_bit_eq_1_out_3, n8_bit_eq_2_out_3, n8_bit_eq_3_out_3, n8_bit_eq_4_out_3,
       n16_bit_eq_1_out_3, n16_bit_gt_1_out_3, n16_bit_gt_2_out_3;

  // Probe on Input_1
  // Probe on Input_2
  _16_bit_GT u_16_bit_gt_1 (.Input_1(Input_1[15:0]), .Input_2(Input_2[15:0]), .out_3(n16_bit_gt_1_out_3));
  _16_bit_GT u_16_bit_gt_2 (.Input_1(Input_1[31:16]), .Input_2(Input_2[31:16]), .out_3(n16_bit_gt_2_out_3));
  _8_bit_EQ u_8_bit_eq_1 (.in_1(Input_1[7:0]), .in_2(Input_2[7:0]), .out_3(n8_bit_eq_1_out_3));
  _8_bit_EQ u_8_bit_eq_2 (.in_1(Input_1[15:8]), .in_2(Input_2[15:8]), .out_3(n8_bit_eq_2_out_3));
  _8_bit_EQ u_8_bit_eq_3 (.in_1(Input_1[23:16]), .in_2(Input_2[23:16]), .out_3(n8_bit_eq_3_out_3));
  _8_bit_EQ u_8_bit_eq_4 (.in_1(Input_1[31:24]), .in_2(Input_2[31:24]), .out_3(n8_bit_eq_4_out_3));
  _16_bit_EQ u_16_bit_eq_1 (.in_1(Input_1[31:16]), .in_2(Input_2[31:16]), .out_3(n16_bit_eq_1_out_3));
  and EQ (EQ_out, n8_bit_eq_1_out_3, n8_bit_eq_2_out_3, n8_bit_eq_3_out_3, n8_bit_eq_4_out_3);
  and and_1 (and_1_out, n16_bit_gt_1_out_3, n16_bit_eq_1_out_3);
  or GT (GT_out, and_1_out, n16_bit_gt_2_out_3);
  or or_1 (out_3, EQ_out, GT_out);
endmodule

module _2_bit_GT (
  input  A0,
  input  A1,
  input  B0,
  input  B1,
  output out_5
);

  wire and_1_out, and_2_out, and_3_out, and_4_out, and_5_out, and_6_out, not_1_out, not_2_out, not_3_out,
       not_4_out;

  not not_1 (not_1_out, A0);
  not not_2 (not_2_out, A1);
  not not_3 (not_3_out, B0);
  not not_4 (not_4_out, B1);
  and and_1 (and_1_out, not_1_out, A1, not_3_out, not_4_out);
  and and_2 (and_2_out, A0, not_2_out, not_3_out, not_4_out);
  and and_3 (and_3_out, A0, A1, not_3_out, not_4_out);
  and and_4 (and_4_out, A0, not_2_out, not_3_out, B1);
  and and_5 (and_5_out, A0, A1, not_3_out, B1);
  and and_6 (and_6_out, A0, A1, B0, not_4_out);
  or or_1 (out_5, and_1_out, and_2_out, and_3_out, and_4_out, and_5_out, and_6_out);
endmodule

module sr_latch_clr (
  input  R,
  input  S,
  input  CLR,
  output Q,
  output nQ
);

  wire nor_1_out, nor_2_out;

  nor nor_1 (nor_1_out, R, nQ);
  nor nor_2 (nor_2_out, Q, S);
  and and_1 (Q, nor_1_out, ~CLR);  // AND_Gate
  or or_1 (nQ, nor_2_out, CLR);
endmodule

module D_Latch_w_reset (
  input  Clock,
  input  D,
  input  CLR,
  output Q,
  output nQ
);

  wire and_1_out, and_2_out;

  and and_1 (and_1_out, ~D, Clock);  // AND_Gate
  and and_2 (and_2_out, D, Clock);
  sr_latch_clr sr_latch_clr_1 (.R(and_1_out), .S(and_2_out), .CLR(CLR), .Q(Q), .nQ(nQ));
endmodule

module D_Flip_Flop (
  input  Clock,
  input  D,
  input  CLR,
  output Q
);

  wire d_latch_w_reset_1_q, not_1_out;

  not not_1 (not_1_out, Clock);
  D_Latch_w_reset d_latch_w_reset_1 (.Clock(not_1_out), .D(D), .CLR(CLR), .Q(d_latch_w_reset_1_q));  // open: nQ
  D_Latch_w_reset d_latch_w_reset_2 (.Clock(Clock), .D(d_latch_w_reset_1_q), .CLR(CLR), .Q(Q));  // open: nQ
endmodule

module _4_bit_GT (
  input  [3:0] in_1,
  input  [3:0] in_2,
  output out_3
);

  wire and_1_out, check_upper_out, n1_bit_eq_1_out_3, n1_bit_eq_2_out_3, n2_bit_gt_1_out_5, n2_bit_gt_2_out_5;

  // Probe on in_1
  // Probe on in_2
  _2_bit_GT u_2_bit_gt_1 (.A0(in_1[1]), .A1(in_1[0]), .B0(in_2[1]), .B1(in_2[0]), .out_5(n2_bit_gt_1_out_5));
  _2_bit_GT u_2_bit_gt_2 (.A0(in_1[3]), .A1(in_1[2]), .B0(in_2[3]), .B1(in_2[2]), .out_5(n2_bit_gt_2_out_5));
  _1_bit_EQ u_1_bit_eq_1 (.in_1(in_2[2]), .in_2(in_1[2]), .out_3(n1_bit_eq_1_out_3));
  _1_bit_EQ u_1_bit_eq_2 (.in_1(in_2[3]), .in_2(in_1[3]), .out_3(n1_bit_eq_2_out_3));
  and check_upper (check_upper_out, n1_bit_eq_1_out_3, n1_bit_eq_2_out_3);
  and and_1 (and_1_out, n2_bit_gt_1_out_5, check_upper_out);
  or or_1 (out_3, and_1_out, n2_bit_gt_2_out_5);
endmodule

module _4_bit_EQ (
  input  [3:0] in_1,
  input  [3:0] in_2,
  output out_3
);

  wire n1_bit_eq_1_out_3, n1_bit_eq_2_out_3, n1_bit_eq_3_out_3, n1_bit_eq_4_out_3;

  _1_bit_EQ u_1_bit_eq_1 (.in_1(in_2[0]), .in_2(in_1[0]), .out_3(n1_bit_eq_1_out_3));
  _1_bit_EQ u_1_bit_eq_2 (.in_1(in_2[1]), .in_2(in_1[1]), .out_3(n1_bit_eq_2_out_3));
  _1_bit_EQ u_1_bit_eq_3 (.in_1(in_2[2]), .in_2(in_1[2]), .out_3(n1_bit_eq_3_out_3));
  _1_bit_EQ u_1_bit_eq_4 (.in_1(in_2[3]), .in_2(in_1[3]), .out_3(n1_bit_eq_4_out_3));
  and and_1 (out_3, n1_bit_eq_1_out_3, n1_bit_eq_2_out_3, n1_bit_eq_3_out_3, n1_bit_eq_4_out_3);
endmodule

module _16_bit_EQ (
  input  [15:0] in_1,
  input  [15:0] in_2,
  output out_3
);

  wire n4_bit_eq_1_out_3, n4_bit_eq_2_out_3, n4_bit_eq_3_out_3, n4_bit_eq_4_out_3;

  _4_bit_EQ u_4_bit_eq_1 (.in_1(in_1[3:0]), .in_2(in_2[3:0]), .out_3(n4_bit_eq_1_out_3));
  _4_bit_EQ u_4_bit_eq_2 (.in_1(in_1[7:4]), .in_2(in_2[7:4]), .out_3(n4_bit_eq_2_out_3));
  _4_bit_EQ u_4_bit_eq_3 (.in_1(in_1[11:8]), .in_2(in_2[11:8]), .out_3(n4_bit_eq_3_out_3));
  _4_bit_EQ u_4_bit_eq_4 (.in_1(in_1[15:12]), .in_2(in_2[15:12]), .out_3(n4_bit_eq_4_out_3));
  and and_1 (out_3, n4_bit_eq_1_out_3, n4_bit_eq_2_out_3, n4_bit_eq_3_out_3, n4_bit_eq_4_out_3);
endmodule

module _16_bit_GT (
  input  [15:0] Input_1,
  input  [15:0] Input_2,
  output out_3
);

  wire and_1_out, n8_bit_eq_1_out_3, n8_bit_gt_1_out_3, n8_bit_gt_2_out_3;

  // Probe on Input_1
  // Probe on Input_2
  _8_bit_GT u_8_bit_gt_1 (.Input_1(Input_1[7:0]), .Input_2(Input_2[7:0]), .out_3(n8_bit_gt_1_out_3));
  _8_bit_GT u_8_bit_gt_2 (.Input_1(Input_1[15:8]), .Input_2(Input_2[15:8]), .out_3(n8_bit_gt_2_out_3));
  _8_bit_EQ u_8_bit_eq_1 (.in_1(Input_1[15:8]), .in_2(Input_2[15:8]), .out_3(n8_bit_eq_1_out_3));
  and and_1 (and_1_out, n8_bit_gt_1_out_3, n8_bit_eq_1_out_3);
  or or_1 (out_3, and_1_out, n8_bit_gt_2_out_3);
endmodule

module _32_bit_GT (
  input  [31:0] Input_1,
  input  [31:0] Input_2,
  output out_3
);

  wire and_1_out, n16_bit_eq_1_out_3, n16_bit_gt_1_out_3, n16_bit_gt_2_out_3;

  // Probe on Input_1
  // Probe on Input_2
  _16_bit_GT u_16_bit_gt_1 (.Input_1(Input_1[15:0]), .Input_2(Input_2[15:0]), .out_3(n16_bit_gt_1_out_3));
  _16_bit_GT u_16_bit_gt_2 (.Input_1(Input_1[31:16]), .Input_2(Input_2[31:16]), .out_3(n16_bit_gt_2_out_3));
  _16_bit_EQ u_16_bit_eq_1 (.in_1(Input_1[31:16]), .in_2(Input_2[31:16]), .out_3(n16_bit_eq_1_out_3));
  and and_1 (and_1_out, n16_bit_gt_1_out_3, n16_bit_eq_1_out_3);
  or or_1 (out_3, and_1_out, n16_bit_gt_2_out_3);
endmodule

module _32_bit_LT (
  input  [31:0] Input_1,
  input  [31:0] Input_2,
  output out_3
);

  wire and_1_out, EQ_out, GT_out, n8_bit_eq_1_out_3, n8_bit_eq_2_out_3, n8_bit_eq_3_out_3, n8_bit_eq_4_out_3,
       n16_bit_eq_1_out_3, n16_bit_gt_1_out_3, n16_bit_gt_2_out_3, or_1_out;

  // Probe on Input_1
  // Probe on Input_2
  _16_bit_GT u_16_bit_gt_1 (.Input_1(Input_1[15:0]), .Input_2(Input_2[15:0]), .out_3(n16_bit_gt_1_out_3));
  _16_bit_GT u_16_bit_gt_2 (.Input_1(Input_1[31:16]), .Input_2(Input_2[31:16]), .out_3(n16_bit_gt_2_out_3));
  _8_bit_EQ u_8_bit_eq_1 (.in_1(Input_1[7:0]), .in_2(Input_2[7:0]), .out_3(n8_bit_eq_1_out_3));
  _8_bit_EQ u_8_bit_eq_2 (.in_1(Input_1[15:8]), .in_2(Input_2[15:8]), .out_3(n8_bit_eq_2_out_3));
  _8_bit_EQ u_8_bit_eq_3 (.in_1(Input_1[23:16]), .in_2(Input_2[23:16]), .out_3(n8_bit_eq_3_out_3));
  _8_bit_EQ u_8_bit_eq_4 (.in_1(Input_1[31:24]), .in_2(Input_2[31:24]), .out_3(n8_bit_eq_4_out_3));
  _16_bit_EQ u_16_bit_eq_1 (.in_1(Input_1[31:16]), .in_2(Input_2[31:16]), .out_3(n16_bit_eq_1_out_3));
  and EQ (EQ_out, n8_bit_eq_1_out_3, n8_bit_eq_2_out_3, n8_bit_eq_3_out_3, n8_bit_eq_4_out_3);
  and and_1 (and_1_out, n16_bit_gt_1_out_3, n16_bit_eq_1_out_3);
  or GT (GT_out, and_1_out, n16_bit_gt_2_out_3);
  or or_1 (or_1_out, EQ_out, GT_out);
  not not_1 (out_3, or_1_out);
endmodule

module _4_bit_to_8_bit_sign_extension (
  input  [3:0] in_1,
  output [7:0] out_2
);

  wire not_1_out;

  not not_1 (not_1_out, in_1[3]);
  Multiplexer #(.width(4), .disabled(0)) multiplexer_1 (
    .in0(4'b1111), .in1(4'b0000), .out(out_2[7:4]), .sel(not_1_out), .en(in_1[3]));

  assign out_2[3:0] = in_1;
endmodule

module _8_bit_adder (
  input  C_in,
  input  [7:0] in_2,
  input  [7:0] in_3,
  output [7:0] out_4,
  output C_out
);

  wire n4_bit_adder_1_c_out;

  // Probe on in_2
  // Probe on in_3
  _4_bit_adder u_4_bit_adder_1 (
    .in_2(in_2[3:0]), .in_3(in_3[3:0]), .out_4(out_4[3:0]), .C_in(C_in), .C_out(n4_bit_adder_1_c_out));
  _4_bit_adder u_4_bit_adder_2 (
    .in_2(in_2[7:4]), .in_3(in_3[7:4]), .out_4(out_4[7:4]), .C_in(n4_bit_adder_1_c_out), .C_out(C_out));
  // Probe on out_4
endmodule

module _1_bit_adder (
  input  a_in,
  input  b_in,
  input  c_in,
  output output_1,
  output output_2
);

  wire and_1_out, and_2_out, and_3_out, and_4_out, and_5_out, and_6_out, and_7_out, and_8_out;

  and and_1 (and_1_out, ~a_in, ~b_in, c_in);  // AND_Gate
  and and_2 (and_2_out, ~a_in, b_in, ~c_in);  // AND_Gate
  and and_3 (and_3_out, a_in, ~b_in, ~c_in);  // AND_Gate
  and and_4 (and_4_out, a_in, b_in, c_in);
  and and_5 (and_5_out, ~a_in, b_in, c_in);  // AND_Gate
  and and_6 (and_6_out, a_in, ~b_in, c_in);  // AND_Gate
  and and_7 (and_7_out, a_in, b_in, ~c_in);  // AND_Gate
  and and_8 (and_8_out, a_in, b_in);
  or or_1 (output_1, and_1_out, and_2_out, and_3_out, and_4_out);
  or or_2 (output_2, and_5_out, and_6_out, and_7_out, and_8_out);
endmodule

module _4_bit_adder (
  input  C_in,
  input  [3:0] in_2,
  input  [3:0] in_3,
  output [3:0] out_4,
  output C_out
);

  wire n1_bit_adder_1_output_2, n1_bit_adder_2_output_2, n1_bit_adder_3_output_2;

  // Probe on in_2
  // Probe on in_3
  _1_bit_adder u_1_bit_adder_1 (
    .output_1(out_4[0]), .output_2(n1_bit_adder_1_output_2), .a_in(C_in), .b_in(in_2[0]), .c_in(in_3[0]));
  _1_bit_adder u_1_bit_adder_2 (
    .output_1(out_4[1]), .output_2(n1_bit_adder_2_output_2), .a_in(n1_bit_adder_1_output_2), .b_in(in_2[1]),
    .c_in(in_3[1]));
  _1_bit_adder u_1_bit_adder_3 (
    .output_1(out_4[2]), .output_2(n1_bit_adder_3_output_2), .a_in(n1_bit_adder_2_output_2), .b_in(in_2[2]),
    .c_in(in_3[2]));
  _1_bit_adder u_1_bit_adder_4 (
    .output_1(out_4[3]), .output_2(C_out), .a_in(n1_bit_adder_3_output_2), .b_in(in_2[3]), .c_in(in_3[3]));
  // Probe on out_4
endmodule

module Y2_Z2 (
  input  [7:0] in_1,
  output [2:0] Y2_output,
  output [2:0] Z2_output
);

  Y2_0 y2_0_1 (
    .A7(in_1[7]), .A6(in_1[6]), .A5(in_1[5]), .A4(in_1[4]), .A3(in_1[3]), .A2(in_1[2]), .A1(in_1[1]),
    .A0(in_1[0]), .Y2(Y2_output[2]), .Y1(Y2_output[1]), .Y0(Y2_output[0]));  // open: NONE
  Z2_0 z2_0_1 (
    .A7(in_1[7]), .A6(in_1[6]), .A5(in_1[5]), .A4(in_1[4]), .A3(in_1[3]), .A2(in_1[2]), .A1(in_1[1]),
    .A0(in_1[0]), .Z2(Z2_output[2]), .Z1(Z2_output[1]), .Z0(Z2_output[0]));
  // Probe on Y2_output
  // Probe on Z2_output
endmodule

module ROM_LDR (
  input  CLR,
  output [7:0] out_2
);

  wire clock_1_out, not_1_out;
  wire [3:0] n4_bit_counter_1_out_3;
  wire [7:0] register_file_1_out_6, register_file_1_out_7, register_file_1_out_8, register_file_1_out_9,
       register_file_1_out_10, register_file_1_out_11, register_file_1_out_12, register_file_1_out_13;

  Clock clock_1 (.out(clock_1_out));
  // Probe on n4_bit_counter_1_out_3
  not not_1 (not_1_out, clock_1_out);
  _4_bit_counter u_4_bit_counter_1 (.CLK(clock_1_out), .CLR(CLR), .out_3(n4_bit_counter_1_out_3));
  ROM #(.addrWidth(4)) rom_1 (.addr(n4_bit_counter_1_out_3), .data(out_2), .sel(1'b1));
  // Probe on n4_bit_counter_1_out_3[2:0]
  // Probe on out_2
  DotMatrix #(.inputtype("row"), .matrixcols(8), .matrixrows(8)) dotmatrix_1 (
    .row0(register_file_1_out_6), .row1(register_file_1_out_7), .row2(register_file_1_out_8),
    .row3(register_file_1_out_9), .row4(register_file_1_out_10), .row5(register_file_1_out_11),
    .row6(register_file_1_out_12), .row7(register_file_1_out_13));
  Register_File register_file_1 (
    .CLK(not_1_out), .Data(out_2), .WE(1'b1), ._3_to_8_decoder(n4_bit_counter_1_out_3[2:0]), .CLR(CLR),
    .out_6(register_file_1_out_6), .out_7(register_file_1_out_7), .out_8(register_file_1_out_8),
    .out_9(register_file_1_out_9), .out_10(register_file_1_out_10), .out_11(register_file_1_out_11),
    .out_12(register_file_1_out_12), .out_13(register_file_1_out_13));

  // Notes on the sheet:
  //   contents of rom_1 (hex, n*v repeats v):
  //   0 ee 8a 8a ce 88 88 e8 0 24 24 0 42 24 18
endmodule

module _4_bit_register (
  input  CLK,
  input  [3:0] in_2,
  input  EN,
  input  CLR,
  output [3:0] out_5
);

  _1_bit_register u_1_bit_register_1 (.Clock(CLK), .D(in_2[0]), .EN(EN), .CLR(CLR), .Q(out_5[0]));
  _1_bit_register u_1_bit_register_2 (.Clock(CLK), .D(in_2[1]), .EN(EN), .CLR(CLR), .Q(out_5[1]));
  _1_bit_register u_1_bit_register_3 (.Clock(CLK), .D(in_2[2]), .EN(EN), .CLR(CLR), .Q(out_5[2]));
  _1_bit_register u_1_bit_register_4 (.Clock(CLK), .D(in_2[3]), .EN(EN), .CLR(CLR), .Q(out_5[3]));
endmodule

module _4_bit_counter (
  input  CLK,
  input  CLR,
  output [3:0] out_3
);

  wire [3:0] n4_bit_adder_1_out_4;

  _4_bit_register u_4_bit_register_1 (.CLK(CLK), .in_2(n4_bit_adder_1_out_4), .EN(1'b1), .CLR(CLR), .out_5(out_3));
  _4_bit_adder u_4_bit_adder_1 (
    .in_2(out_3), .in_3(4'b0001), .out_4(n4_bit_adder_1_out_4), .C_in(1'b0));  // open: C_out
endmodule

module _1_bit_register (
  input  Clock,
  input  D,
  input  EN,
  input  CLR,
  output Q
);

  wire and_1_out;

  and and_1 (and_1_out, Clock, EN);
  D_Flip_Flop d_ff_1 (.Clock(and_1_out), .D(D), .CLR(CLR), .Q(Q));
endmodule

module _8_bit_register (
  input  CLK,
  input  [7:0] in_2,
  input  EN,
  input  CLR,
  output [7:0] out_5
);

  _4_bit_register u_4_bit_register_1 (.CLK(CLK), .in_2(in_2[3:0]), .EN(EN), .CLR(CLR), .out_5(out_5[3:0]));
  _4_bit_register u_4_bit_register_2 (.CLK(CLK), .in_2(in_2[7:4]), .EN(EN), .CLR(CLR), .out_5(out_5[7:4]));
endmodule

module Register_File (
  input  CLK,
  input  [7:0] Data,
  input  WE,
  input  [2:0] _3_to_8_decoder,
  input  CLR,
  output [7:0] out_6,
  output [7:0] out_7,
  output [7:0] out_8,
  output [7:0] out_9,
  output [7:0] out_10,
  output [7:0] out_11,
  output [7:0] out_12,
  output [7:0] out_13
);

  wire and_1_out, and_2_out, and_3_out, and_4_out, and_5_out, and_6_out, and_7_out, and_8_out,
       n3_to_8_decoder_1_y0, n3_to_8_decoder_1_y1, n3_to_8_decoder_1_y2, n3_to_8_decoder_1_y3,
       n3_to_8_decoder_1_y4, n3_to_8_decoder_1_y5, n3_to_8_decoder_1_y6, n3_to_8_decoder_1_y7;

  _3_to_8_decoder u_3_to_8_decoder_1 (
    .Y0(n3_to_8_decoder_1_y0), .Y1(n3_to_8_decoder_1_y1), .Y2(n3_to_8_decoder_1_y2),
    .Y3(n3_to_8_decoder_1_y3), .Y4(n3_to_8_decoder_1_y4), .Y5(n3_to_8_decoder_1_y5),
    .Y6(n3_to_8_decoder_1_y6), .Y7(n3_to_8_decoder_1_y7), .D2(_3_to_8_decoder[2]), .D1(_3_to_8_decoder[1]),
    .D0(_3_to_8_decoder[0]));
  and and_1 (and_1_out, WE, n3_to_8_decoder_1_y0);
  and and_2 (and_2_out, WE, n3_to_8_decoder_1_y1);
  and and_3 (and_3_out, WE, n3_to_8_decoder_1_y2);
  and and_4 (and_4_out, WE, n3_to_8_decoder_1_y3);
  and and_5 (and_5_out, WE, n3_to_8_decoder_1_y4);
  and and_6 (and_6_out, WE, n3_to_8_decoder_1_y5);
  and and_7 (and_7_out, WE, n3_to_8_decoder_1_y6);
  and and_8 (and_8_out, WE, n3_to_8_decoder_1_y7);
  _8_bit_register u_8_bit_register_1 (.CLK(CLK), .in_2(Data), .EN(and_1_out), .CLR(CLR), .out_5(out_6));
  _8_bit_register u_8_bit_register_2 (.CLK(CLK), .in_2(Data), .EN(and_2_out), .CLR(CLR), .out_5(out_7));
  _8_bit_register u_8_bit_register_3 (.CLK(CLK), .in_2(Data), .EN(and_3_out), .CLR(CLR), .out_5(out_8));
  _8_bit_register u_8_bit_register_4 (.CLK(CLK), .in_2(Data), .EN(and_4_out), .CLR(CLR), .out_5(out_9));
  _8_bit_register u_8_bit_register_5 (.CLK(CLK), .in_2(Data), .EN(and_5_out), .CLR(CLR), .out_5(out_10));
  _8_bit_register u_8_bit_register_6 (.CLK(CLK), .in_2(Data), .EN(and_6_out), .CLR(CLR), .out_5(out_11));
  _8_bit_register u_8_bit_register_7 (.CLK(CLK), .in_2(Data), .EN(and_7_out), .CLR(CLR), .out_5(out_12));
  _8_bit_register u_8_bit_register_8 (.CLK(CLK), .in_2(Data), .EN(and_8_out), .CLR(CLR), .out_5(out_13));
endmodule

module _3_to_8_decoder (
  input  D2,
  input  D1,
  input  D0,
  output Y0,
  output Y1,
  output Y2,
  output Y3,
  output Y4,
  output Y5,
  output Y6,
  output Y7
);

  wire not_1_out, not_2_out, not_3_out;

  not not_1 (not_1_out, D2);
  not not_2 (not_2_out, D1);
  not not_3 (not_3_out, D0);
  and and_1 (Y0, not_1_out, not_2_out, not_3_out);
  and and_2 (Y1, D0, not_2_out, not_1_out);
  and and_3 (Y2, not_3_out, D1, not_1_out);
  and and_4 (Y3, D0, D1, not_1_out);
  and and_5 (Y4, not_3_out, not_2_out, D2);
  and and_6 (Y5, D0, not_2_out, D2);
  and and_7 (Y6, not_3_out, D1, D2);
  and and_8 (Y7, D0, D1, D2);
endmodule

module ALU (
  input  MOV_indicate,
  input  MVN_indicate,
  input  [1:0] ALU_Control,
  input  [31:0] B,
  input  [31:0] A,
  output [31:0] Result,
  output [3:0] ALU_Flags
);

  wire adder_1_cout, multiplexer_3_out, not_2_out, xnor_1_out, xor_1_out;
  wire [31:0] adder_1_out, and_1_out, multiplexer_1_out, multiplexer_2_out, not_1_out, or_1_out;

  // Probe on B
  // Probe on A
  Multiplexer #(.width(32), .disabled(0), .enable("false")) multiplexer_1 (
    .in0(A), .in1({32{1'b0}}), .out(multiplexer_1_out), .sel(MOV_indicate));
  assign not_1_out = ~B;  // NOT_Gate not_1, 32 bits wide
  Multiplexer #(.width(32), .disabled(0), .enable("false")) multiplexer_2 (
    .in0(B), .in1(not_1_out), .out(multiplexer_2_out), .sel(ALU_Control[0]));
  // Probe on multiplexer_2_out
  Multiplexer #(.disabled(0), .enable("false")) multiplexer_3 (
    .in0(ALU_Control[0]), .in1(1'b0), .out(multiplexer_3_out), .sel(MVN_indicate));
  not not_2 (not_2_out, ALU_Control[1]);
  xor xor_1 (xor_1_out, adder_1_out[31], multiplexer_1_out[31]);
  NotExactlyOne xnor_1 (.out(xnor_1_out), .in0(B[31]), .in1(multiplexer_1_out[31]), .in2(ALU_Control[0]));
  // Probe on adder_1_out
  Adder #(.width(32)) adder_1 (
    .a(multiplexer_2_out), .b(multiplexer_1_out), .out(adder_1_out), .cin(multiplexer_3_out),
    .cout(adder_1_cout));
  assign and_1_out = B & multiplexer_1_out;  // AND_Gate and_1, 32 bits wide
  assign or_1_out = B | multiplexer_1_out;  // OR_Gate or_1, 32 bits wide
  Multiplexer #(.select(2), .width(32), .disabled(0), .enable("false")) multiplexer_4 (
    .in0(adder_1_out), .in1(adder_1_out), .in2(and_1_out), .in3(or_1_out),
    .out({ALU_Flags[3], Result[30:0]}), .sel(ALU_Control));
  and and_2 (ALU_Flags[1], adder_1_cout, not_2_out);
  and and_3 (ALU_Flags[0], not_2_out, xor_1_out, xnor_1_out);
  _32_bit_NEG_AND u_32_bit_neg_and_1 (.in_1({ALU_Flags[3], Result[30:0]}), .out_2(ALU_Flags[2]));
  // Probe on {ALU_Flags[3], Result[30:0]}

  assign Result[31] = ALU_Flags[3];

  // Notes on the sheet:
  //   Zero
  //   Negative
  //   Carry
  //   oVerFlow
  //   NZCV
endmodule

module _32_bit_NEG_AND (
  input  [31:0] in_1,
  output out_2
);

  and and_1 (out_2, ~in_1[0], ~in_1[1], ~in_1[2], ~in_1[3], ~in_1[4], ~in_1[5], ~in_1[6], ~in_1[7], ~in_1[8], ~in_1[9], ~in_1[10], ~in_1[11], ~in_1[12], ~in_1[13], ~in_1[14], ~in_1[15], ~in_1[16], ~in_1[17], ~in_1[18], ~in_1[19], ~in_1[20], ~in_1[21], ~in_1[22], ~in_1[23], ~in_1[24], ~in_1[25], ~in_1[26], ~in_1[27], ~in_1[28], ~in_1[29], ~in_1[30], ~in_1[31]);  // AND_Gate
endmodule
