// Logisim project main_emulator.circ as structural Verilog
module main (
  input  in_1,
  input  [1:0] in_2
);

  wire C, CLK, control_unit_1_alusrc, control_unit_1_bl_indicate, control_unit_1_memtoreg,
       control_unit_1_memwrite, control_unit_1_mov_indicate, control_unit_1_mvn_indicate,
       control_unit_1_pcsrc, control_unit_1_regwrite, N, V, Z;
  wire [1:0] control_unit_1_alucontrol, control_unit_1_immsrc, control_unit_1_regsrc;
  wire [3:0] Cond, multiplexer_2_out, multiplexer_3_out;
  wire [27:0] INST;
  wire [31:0] adder_1_out, adder_2_out, alu_1_p6, datamemory_1_rd, extend_1_out_3, multiplexer_1_out,
       multiplexer_4_out, multiplexer_5_out, PC, r0, r1, r2, r3, r4, r5, r6, r7, r8, r9, r10, r11, r12, r13,
       r14, r15, register_file_1_rd1, register_file_1_rd2;

  Clock clock_1 (.out(CLK));
  Multiplexer #(.width(32), .disabled(0), .enable("false")) multiplexer_1 (
    .in0(adder_1_out), .in1(multiplexer_5_out), .out(multiplexer_1_out), .sel(control_unit_1_pcsrc));
  PC pc_1 (.PC(multiplexer_1_out), .PC_2(PC), .CLK(CLK), .CLR(in_1));
  // Probe on N
  Adder #(.width(32)) adder_1 (.a(PC), .b(32'h4), .out(adder_1_out));  // open: cin, cout
  // Probe on Z
  // Probe on C
  // Probe on Cond
  Intruction_Memory intruction_memory_1 (.A(PC), .RD({Cond, INST}), .in_2(in_2));
  // Probe on V
  Multiplexer #(.width(4), .disabled(0), .enable("false")) multiplexer_2 (
    .in0(INST[19:16]), .in1(4'b1111), .out(multiplexer_2_out), .sel(control_unit_1_regsrc[0]));
  // Probe on PC
  // Probe on {Cond, INST}
  // Probe on {Cond, INST}
  Control_Unit control_unit_1 (
    .Cond(Cond), .ALUFlags({N, Z, C, V}), .Op(INST[27:26]), .Funct(INST[25:20]), .Rd(INST[15:12]),
    .PCSrc(control_unit_1_pcsrc), .RegWrite(control_unit_1_regwrite), .MemWrite(control_unit_1_memwrite),
    .MemtoReg(control_unit_1_memtoreg), .ALUSrc(control_unit_1_alusrc), .ImmSrc(control_unit_1_immsrc),
    .RegSrc(control_unit_1_regsrc), .ALUControl(control_unit_1_alucontrol), .CLK(CLK), .CLR(in_1),
    .MOV_indicate(control_unit_1_mov_indicate), .BL_indicate(control_unit_1_bl_indicate),
    .MVN_indicate(control_unit_1_mvn_indicate));
  Multiplexer #(.width(4), .disabled(0), .enable("false")) multiplexer_3 (
    .in0(INST[3:0]), .in1(INST[15:12]), .out(multiplexer_3_out), .sel(control_unit_1_regsrc[1]));
  Adder #(.width(32)) adder_2 (.a(adder_1_out), .b(32'h4), .out(adder_2_out));  // open: cin, cout
  // Probe on r0
  // Probe on r1
  // Probe on r2
  // Probe on r3
  // Probe on r4
  // Probe on r5
  // Probe on r6
  // Probe on r7
  Register_File register_file_1 (
    .A1(multiplexer_2_out), .A2(multiplexer_3_out), .A3(INST[15:12]), .WD3(multiplexer_5_out),
    .PC(adder_2_out), .RD1(register_file_1_rd1), .RD2(register_file_1_rd2), .R0(r0), .R1(r1), .R2(r2),
    .R3(r3), .R4(r4), .R5(r5), .R6(r6), .R7(r7), .R8(r8), .R9(r9), .R10(r10), .R11(r11), .R12(r12),
    .R13(r13), .R14(r14), .R15(r15), .CLK(CLK), .WE(control_unit_1_regwrite), .CLR(in_1),
    .BL_indicate(control_unit_1_bl_indicate));
  extend extend_1 (.in_2(INST[23:0]), .out_3(extend_1_out_3), .ImmSrc(control_unit_1_immsrc));
  // Probe on r8
  // Probe on r9
  // Probe on r10
  // Probe on r11
  // Probe on r12
  // Probe on r13
  // Probe on r14
  // Probe on r15
  Multiplexer #(.width(32), .disabled(0), .enable("false")) multiplexer_4 (
    .in0(register_file_1_rd2), .in1(extend_1_out_3), .out(multiplexer_4_out), .sel(control_unit_1_alusrc));
  // Probe on r0
  // Probe on r1
  // Probe on r2
  // Probe on r3
  // Probe on r4
  // Probe on r5
  // Probe on r6
  // Probe on r7
  // Homework02_ALU alu_1: pin names not known; wires that end beside it: control_unit_1_mov_indicate, control_unit_1_mvn_indicate, register_file_1_rd1, multiplexer_4_out, control_unit_1_alucontrol, alu_1_p6, {N, Z, C, V}
  // Probe on r8
  // Probe on r9
  // Probe on r10
  // Probe on r11
  // Probe on r12
  // Probe on r13
  // Probe on r14
  // Probe on r15
  DataMemory datamemory_1 (
    .A(alu_1_p6), .WD(register_file_1_rd2), .RD(datamemory_1_rd), .CLK(CLK), .WE(control_unit_1_memwrite),
    .CLR(in_1));
  Multiplexer #(.width(32), .disabled(0), .enable("false")) multiplexer_5 (
    .in0(alu_1_p6), .in1(datamemory_1_rd), .out(multiplexer_5_out), .sel(control_unit_1_memtoreg));

  // Other names for the same wires on the sheet: CLR = in_1; INST[31:28] = Cond; Select_Program[1:0] = in_2

  // Notes on the sheet:
  //   00 -------- sum_array_a.s
  //   01 --------- find_max_a.s
  //   10 ----------- fib_iter_a.s
  //   11 ----------- fib_rec_a.s
  //   PC + 4
  //   Flags
  //   Condition
  //   PC + 8
  //   PC
  //   Instruction
  //   MemtoReg
  //   Mem Write
  //   ALUControl
  //   MOV_indicate
  //   ALUsrc
  //   IMM scr
  //   RegWrite
  //   BL_indicate
  //   MVN_indicate
  //   Hexidecimal
  //   Register States
  //   ALU
  //   Decimal
endmodule

module Intruction_Memory (
  input  [31:0] A,
  input  [1:0] in_2,
  output [31:0] RD
);

  wire comparator_1_eq;
  wire [3:0] multiplexer_1_out_3;
  wire [7:0] divider_1_out;
  wire [23:0] multiplexer_1_out;
  wire [31:0] rom_1_data, rom_2_data, rom_3_data, rom_4_data;
  wire [31:28] multiplexer_1_out_2;

  Divider divider_1 (.a(A[7:0]), .b(8'h4), .out(divider_1_out));  // open: upper, rem
  ROM #(.dataWidth(32)) rom_1 (.addr(divider_1_out), .data(rom_1_data));  // open: sel
  ROM #(.dataWidth(32)) rom_2 (.addr(divider_1_out), .data(rom_2_data));  // open: sel
  ROM #(.dataWidth(32)) rom_3 (.addr(divider_1_out), .data(rom_3_data));  // open: sel
  ROM #(.dataWidth(32)) rom_4 (.addr(divider_1_out), .data(rom_4_data));  // open: sel
  Multiplexer #(.select(2), .width(32), .disabled(0), .enable("false")) multiplexer_1 (
    .in0(rom_1_data), .in1(rom_2_data), .in2(rom_3_data), .in3(rom_4_data),
    .out({multiplexer_1_out_2, multiplexer_1_out, multiplexer_1_out_3}), .sel(in_2));
  Comparator #(.width(24), .mode("unsigned")) comparator_1 (
    .a(multiplexer_1_out), .b(24'h12fff1), .eq(comparator_1_eq));  // open: gt, lt
  Multiplexer #(.width(32), .disabled(0), .enable("false")) multiplexer_2 (
    .in0({multiplexer_1_out_2, multiplexer_1_out, multiplexer_1_out_3}),
    .in1({28'he1a0f00, multiplexer_1_out_3}), .out(RD), .sel(comparator_1_eq));

  // Notes on the sheet:
  //   sum_array_a.s
  //   find_max_a.s
  //   fib_iter_a.s
  //   fib_rec_a.s
  //   contents of rom_1 (hex, n*v repeats v):
  //   e3a0dc01 e24dd004 e3a00000 e58d0000 e24dd004 e3a00001 e58d0000 e24dd004 e3a00002 e58d0000 e24dd004
  //   e3a00003 e58d0000 e1a0000d e3a01005 eb000000 ea000018 e24dd004 e58d6000 e24dd004 e58d5000 e24dd004
  //   e58d4000 e3a05000 e3a02000 e3a03000 e1550001 a000005 e0806002 e5964000 e2822004 e0833004 e2855001
  //   eafffff7 e59d4000 e28dd004 e59d5000 e28dd004 e59d6000 e28dd004 e1a00003 e12fff1e eafffffe
  //   contents of rom_2 (hex, n*v repeats v):
  //   e3a0dc01 e24dd004 e3a00000 e58d0000 e24dd004 e3a00001 e58d0000 e24dd004 e3a00002 e58d0000 e24dd004
  //   e3a00003 e58d0000 e1a0000d e3a01005 eb000000 ea000019 e24dd004 e58d6000 e24dd004 e58d5000 e24dd004
  //   e58d4000 e5903000 e3a05000 e3a02000 e1550001 a000006 e0806002 e5964000 e2822004 e1540003 c1a03004
  //   e2855001 eafffff6 e59d4000 e28dd004 e59d5000 e28dd004 e59d6000 e28dd004 e1a00003 e12fff1e eafffffe
  //   contents of rom_3 (hex, n*v repeats v):
  //   e3a0d0ff e2800007 eb000000 ea000015 e24dd008 e58d4000 e3a02001 e3a03000 e3a04000 e3500000 a00000b
  //   e3500001 3a00001 a000008 e3a01002 e1510000 c1a00004 ca000004 e0824003 e1a03002 e1a02004 e2811001
  //   eafffff7 e59d4000 e28dd008 e12fff1e eafffffe
  //   contents of rom_4 (hex, n*v repeats v):
  //   e3a0d0ff e2800008 eb000000 ea00001b e24dd004 e58d4000 e24dd004 e58d5000 e24dd004 e58d6000 e24dd004
  //   e58de000 e3500001 ca000000 ea000007 e2404001 e1a00004 ebfffff1 e1a05000 e2440001 ebffffee e1a06000
  //   e0850006 e59de000 e28dd004 e59d6000 e28dd004 e59d5000 e28dd004 e59d4000 e28dd004 e1a0f00e eafffffe
endmodule

module PC (
  input  CLK,
  input  [31:0] PC,
  input  CLR,
  output [31:0] PC_2
);

  Register #(.width(32)) register_1 (.D(PC), .en(1'b1), .Q(PC_2), .clk(CLK), .clr(CLR));
endmodule

module _4_bit_decoder (
  input  D2,
  input  D2_2,
  input  D1,
  input  D0,
  output Y0,
  output Y1,
  output Y2,
  output Y3,
  output Y4,
  output Y5,
  output Y6,
  output Y7,
  output Y8,
  output Y9,
  output Y10,
  output Y11,
  output Y12,
  output Y13,
  output Y14,
  output Y15
);

  wire not_1_out, not_2_out, not_3_out, not_4_out;

  not not_1 (not_1_out, D2);
  not not_2 (not_2_out, D2_2);
  not not_3 (not_3_out, D1);
  not not_4 (not_4_out, D0);
  and and_1 (Y0, not_4_out, not_3_out, not_2_out, not_1_out);
  and and_2 (Y1, D0, not_3_out, not_2_out, not_1_out);
  and and_3 (Y2, not_4_out, D1, not_2_out, not_1_out);
  and and_4 (Y3, D0, D1, not_2_out, not_1_out);
  and and_5 (Y4, not_4_out, not_3_out, D2_2, not_1_out);
  and and_6 (Y5, D0, not_3_out, D2_2, not_1_out);
  and and_7 (Y6, not_4_out, D1, D2_2, not_1_out);
  and and_8 (Y7, D0, D1, D2_2, not_1_out);
  and and_9 (Y8, not_4_out, not_3_out, not_2_out, D2);
  and and_10 (Y9, D0, not_3_out, not_2_out, D2);
  and and_11 (Y10, not_4_out, D1, not_2_out, D2);
  and and_12 (Y11, D0, D1, not_2_out, D2);
  and and_13 (Y12, not_4_out, not_3_out, D2_2, D2);
  and and_14 (Y13, D0, not_3_out, D2_2, D2);
  and and_15 (Y14, not_4_out, D1, D2_2, D2);
  and and_16 (Y15, D0, D1, D2_2, D2);
endmodule

module Register_File (
  input  CLK,
  input  WE,
  input  [3:0] A1,
  input  [3:0] A2,
  input  BL_indicate,
  input  [3:0] A3,
  input  [31:0] WD3,
  input  [31:0] PC,
  input  CLR,
  output [31:0] RD1,
  output [31:0] RD2,
  output [31:0] R0,
  output [31:0] R1,
  output [31:0] R2,
  output [31:0] R3,
  output [31:0] R4,
  output [31:0] R5,
  output [31:0] R6,
  output [31:0] R7,
  output [31:0] R8,
  output [31:0] R9,
  output [31:0] R10,
  output [31:0] R11,
  output [31:0] R12,
  output [31:0] R13,
  output [31:0] R14,
  output [31:0] R15
);

  wire and_1_out, and_2_out, and_3_out, and_4_out, and_5_out, and_6_out, and_7_out, and_8_out, and_9_out,
       and_10_out, and_11_out, and_12_out, and_13_out, and_14_out, and_15_out, n4_bit_decoder_1_y0,
       n4_bit_decoder_1_y1, n4_bit_decoder_1_y2, n4_bit_decoder_1_y3, n4_bit_decoder_1_y4,
       n4_bit_decoder_1_y5, n4_bit_decoder_1_y6, n4_bit_decoder_1_y7, n4_bit_decoder_1_y8,
       n4_bit_decoder_1_y9, n4_bit_decoder_1_y10, n4_bit_decoder_1_y11, n4_bit_decoder_1_y12,
       n4_bit_decoder_1_y13, n4_bit_decoder_1_y14;
  wire [3:0] multiplexer_1_out;
  wire [31:0] multiplexer_2_out, subtractor_1_out;

  // Probe on A3
  // Probe on 4'b1110
  Multiplexer #(.width(4), .disabled(0), .enable("false")) multiplexer_1 (
    .in0(A3), .in1(4'b1110), .out(multiplexer_1_out), .sel(BL_indicate));
  Subtractor #(.width(32)) subtractor_1 (.a(PC), .b(32'h4), .out(subtractor_1_out));  // open: bin, bout
  // Probe on PC
  _4_bit_decoder u_4_bit_decoder_1 (
    .Y0(n4_bit_decoder_1_y0), .Y1(n4_bit_decoder_1_y1), .Y2(n4_bit_decoder_1_y2), .Y3(n4_bit_decoder_1_y3),
    .Y4(n4_bit_decoder_1_y4), .Y5(n4_bit_decoder_1_y5), .Y6(n4_bit_decoder_1_y6), .Y7(n4_bit_decoder_1_y7),
    .Y8(n4_bit_decoder_1_y8), .Y9(n4_bit_decoder_1_y9), .Y10(n4_bit_decoder_1_y10),
    .Y11(n4_bit_decoder_1_y11), .Y12(n4_bit_decoder_1_y12), .Y13(n4_bit_decoder_1_y13),
    .Y14(n4_bit_decoder_1_y14), .D2(multiplexer_1_out[3]), .D2_2(multiplexer_1_out[2]),
    .D1(multiplexer_1_out[1]), .D0(multiplexer_1_out[0]));  // open: Y15
  Multiplexer #(.width(32), .disabled(0), .enable("false")) multiplexer_2 (
    .in0(WD3), .in1(subtractor_1_out), .out(multiplexer_2_out), .sel(BL_indicate));
  // Probe on subtractor_1_out
  and and_1 (and_1_out, n4_bit_decoder_1_y0, WE);
  and and_2 (and_2_out, n4_bit_decoder_1_y1, WE);
  and and_3 (and_3_out, n4_bit_decoder_1_y2, WE);
  and and_4 (and_4_out, n4_bit_decoder_1_y3, WE);
  and and_5 (and_5_out, n4_bit_decoder_1_y4, WE);
  and and_6 (and_6_out, n4_bit_decoder_1_y5, WE);
  and and_7 (and_7_out, n4_bit_decoder_1_y6, WE);
  and and_8 (and_8_out, n4_bit_decoder_1_y7, WE);
  and and_9 (and_9_out, n4_bit_decoder_1_y8, WE);
  and and_10 (and_10_out, n4_bit_decoder_1_y9, WE);
  and and_11 (and_11_out, n4_bit_decoder_1_y10, WE);
  and and_12 (and_12_out, n4_bit_decoder_1_y11, WE);
  and and_13 (and_13_out, n4_bit_decoder_1_y12, WE);
  and and_14 (and_14_out, n4_bit_decoder_1_y13, WE);
  and and_15 (and_15_out, n4_bit_decoder_1_y14, WE);
  Register #(.width(32)) register_1 (.D(multiplexer_2_out), .en(and_1_out), .Q(R0), .clk(CLK), .clr(CLR));
  Register #(.width(32)) register_2 (.D(multiplexer_2_out), .en(and_2_out), .Q(R1), .clk(CLK), .clr(CLR));
  Register #(.width(32)) register_3 (.D(multiplexer_2_out), .en(and_3_out), .Q(R2), .clk(CLK), .clr(CLR));
  Register #(.width(32)) register_4 (.D(multiplexer_2_out), .en(and_4_out), .Q(R3), .clk(CLK), .clr(CLR));
  Register #(.width(32)) register_5 (.D(multiplexer_2_out), .en(and_5_out), .Q(R4), .clk(CLK), .clr(CLR));
  Register #(.width(32)) register_6 (.D(multiplexer_2_out), .en(and_6_out), .Q(R5), .clk(CLK), .clr(CLR));
  Register #(.width(32)) register_7 (.D(multiplexer_2_out), .en(and_7_out), .Q(R6), .clk(CLK), .clr(CLR));
  Register #(.width(32)) register_8 (.D(multiplexer_2_out), .en(and_8_out), .Q(R7), .clk(CLK), .clr(CLR));
  Register #(.width(32)) register_9 (.D(multiplexer_2_out), .en(and_9_out), .Q(R8), .clk(CLK), .clr(CLR));
  Register #(.width(32)) register_10 (.D(multiplexer_2_out), .en(and_10_out), .Q(R9), .clk(CLK), .clr(CLR));
  Register #(.width(32)) register_11 (.D(multiplexer_2_out), .en(and_11_out), .Q(R10), .clk(CLK), .clr(CLR));
  Register #(.width(32)) register_12 (.D(multiplexer_2_out), .en(and_12_out), .Q(R11), .clk(CLK), .clr(CLR));
  Register #(.width(32)) register_13 (.D(multiplexer_2_out), .en(and_13_out), .Q(R12), .clk(CLK), .clr(CLR));
  Register #(.width(32)) register_14 (.D(multiplexer_2_out), .en(and_14_out), .Q(R13), .clk(CLK), .clr(CLR));
  Register #(.width(32)) register_15 (.D(multiplexer_2_out), .en(and_15_out), .Q(R14), .clk(CLK), .clr(CLR));
  Multiplexer #(.select(4), .width(32), .disabled(0), .enable("false")) multiplexer_3 (
    .in0(R0), .in1(R1), .in2(R2), .in3(R3), .in4(R4), .in5(R5), .in6(R6), .in7(R7), .in8(R8), .in9(R9),
    .in10(R10), .in11(R11), .in12(R12), .in13(R13), .in14(R14), .in15(PC), .out(RD1), .sel(A1));
  Multiplexer #(.select(4), .width(32), .disabled(0), .enable("false")) multiplexer_4 (
    .in0(R0), .in1(R1), .in2(R2), .in3(R3), .in4(R4), .in5(R5), .in6(R6), .in7(R7), .in8(R8), .in9(R9),
    .in10(R10), .in11(R11), .in12(R12), .in13(R13), .in14(R14), .in15(PC), .out(RD2), .sel(A2));

  assign R15 = PC;
endmodule

module _32_bit_register (
  input  CLK,
  input  [31:0] in_2,
  input  WE,
  input  CLR,
  output [31:0] out_5
);

  // _8_bit_register 8_bit_register_1: pin names not known; wires that end beside it: CLK, in_2[7:0], WE, CLR, out_5[7:0]
  // _8_bit_register 8_bit_register_2: pin names not known; wires that end beside it: CLK, in_2[15:8], WE, CLR, out_5[15:8]
  // _8_bit_register 8_bit_register_3: pin names not known; wires that end beside it: CLK, in_2[23:16], WE, CLR, out_5[23:16]
  // _8_bit_register 8_bit_register_4: pin names not known; wires that end beside it: CLK, in_2[31:24], WE, CLR, out_5[31:24]
endmodule

module _16_bit_adder (
  input  C_in,
  input  [15:0] in_2,
  input  [15:0] in_3,
  output [15:0] out_4,
  output C_out
);

  wire n8_bit_adder_1_p4;

  // Probe on in_2
  // Probe on in_3
  // _8_bit_adder 8_bit_adder_1: pin names not known; wires that end beside it: in_2[7:0], in_3[7:0], C_in, n8_bit_adder_1_p4, out_4[7:0]
  // _8_bit_adder 8_bit_adder_2: pin names not known; wires that end beside it: in_2[15:8], in_3[15:8], n8_bit_adder_1_p4, C_out, out_4[15:8]
  // Probe on out_4
endmodule

module _32_bit_adder (
  input  C_in,
  input  [31:0] in_2,
  input  [31:0] in_3,
  output [31:0] out_4,
  output C_out
);

  wire n16_bit_adder_1_c_out;

  // Probe on in_2
  // Probe on in_3
  _16_bit_adder u_16_bit_adder_1 (
    .in_2(in_2[15:0]), .in_3(in_3[15:0]), .C_in(C_in), .C_out(n16_bit_adder_1_c_out), .out_4(out_4[15:0]));
  _16_bit_adder u_16_bit_adder_2 (
    .in_2(in_2[31:16]), .in_3(in_3[31:16]), .C_in(n16_bit_adder_1_c_out), .C_out(C_out), .out_4(out_4[31:16]));
  // Probe on out_4
endmodule

module DataMemory (
  input  WE,
  input  CLK,
  input  [31:0] A,
  input  [31:0] WD,
  input  CLR,
  output [31:0] RD
);

  wire not_1_out;

  // Probe on A[9:2]
  // Probe on WD
  not not_1 (not_1_out, WE);
  RAM #(.dataWidth(32), .bus("separate")) ram_1 (
    .addr(A[9:2]), .din(WD), .data(RD), .str(WE), .sel(1'b1), .clk(CLK), .ld(not_1_out), .clr(CLR));
  // Probe on RD
endmodule

module extend (
  input  [1:0] ImmSrc,
  input  [23:0] in_2,
  output [31:0] out_3
);

  wire [23:0] shifter_1_out;
  wire [31:0] bit_extender_1_out, bit_extender_2_out, bit_extender_3_out;

  Shifter #(.width(24)) shifter_1 (.in(in_2), .\dist (5'b00010), .out(shifter_1_out));
  assign bit_extender_1_out = {{24{1'b0}}, in_2[7:0]};  // Bit_Extender bit_extender_1
  assign bit_extender_2_out = {{20{1'b0}}, in_2[11:0]};  // Bit_Extender bit_extender_2
  assign bit_extender_3_out = {{8{shifter_1_out[23]}}, shifter_1_out};  // Bit_Extender bit_extender_3
  Multiplexer #(.select(2), .width(32), .disabled(0), .enable("false")) multiplexer_1 (
    .in0(bit_extender_1_out), .in1(bit_extender_2_out), .in2(bit_extender_3_out), .out(out_3), .sel(ImmSrc));  // open: in3
endmodule

module main_decoder (
  input  [5:0] in_1,
  input  [1:0] Op,
  output Branch,
  output RegW,
  output MemW,
  output MemToReg,
  output ALUSrc,
  output [1:0] ImmSrc,
  output [1:0] RegSrc,
  output BL_indicate,
  output ALUOp
);

  wire and_1_out, and_2_out, B_out, comparator_1_eq, comparator_2_eq, comparator_3_eq, comparator_4_eq,
       DP_Imm_out, DP_Reg_out, not_1_out, not_2_out, not_3_out, not_4_out, not_5_out, or_1_out, or_4_out,
       or_5_out, or_6_out, or_9_out, or_10_out;
  wire [1:0] multiplexer_1_out, multiplexer_4_out;

  not not_1 (not_1_out, in_1[5]);
  not not_2 (not_2_out, in_1[0]);
  Comparator #(.width(4)) comparator_1 (.a(in_1[4:1]), .b(4'b1000), .eq(comparator_1_eq));  // open: gt, lt
  Comparator #(.width(4)) comparator_2 (.a(in_1[4:1]), .b(4'b1001), .eq(comparator_2_eq));  // open: gt, lt
  Comparator #(.width(4)) comparator_3 (.a(in_1[4:1]), .b(4'b1010), .eq(comparator_3_eq));  // open: gt, lt
  Comparator #(.width(4)) comparator_4 (.a(in_1[4:1]), .b(4'b1011), .eq(comparator_4_eq));  // open: gt, lt
  not not_3 (not_3_out, Op[1]);
  or or_1 (or_1_out, comparator_1_eq, comparator_2_eq, comparator_3_eq, comparator_4_eq);
  not not_4 (not_4_out, or_1_out);
  not not_5 (not_5_out, Op[0]);
  and DP_Reg (DP_Reg_out, not_5_out, not_3_out, not_1_out);
  and DP_Imm (DP_Imm_out, not_5_out, not_3_out, in_1[5]);
  and STR (MemW, Op[0], not_3_out, not_2_out);
  and LDR (MemToReg, Op[0], not_3_out, in_1[0]);
  and B (B_out, not_5_out, Op[1]);
  and BL (BL_indicate, not_5_out, Op[1], in_1[4]);
  and and_1 (and_1_out, not_4_out, DP_Reg_out);
  or or_2 (ALUOp, DP_Reg_out, DP_Imm_out);
  and and_2 (and_2_out, not_4_out, DP_Imm_out);
  or or_3 (Branch, B_out, BL_indicate);
  or or_4 (or_4_out, MemToReg, MemW);
  or or_5 (or_5_out, B_out, BL_indicate);
  or or_6 (or_6_out, B_out, BL_indicate);
  or or_7 (RegW, and_1_out, and_2_out, MemToReg, BL_indicate);
  or or_8 (ALUSrc, DP_Imm_out, MemW, MemToReg, B_out, BL_indicate);
  or or_9 (or_9_out, DP_Reg_out, DP_Imm_out);
  or or_10 (or_10_out, DP_Reg_out, MemToReg, DP_Imm_out);
  Multiplexer #(.width(2), .disabled(0), .enable("false")) multiplexer_1 (
    .in1(2'b00), .out(multiplexer_1_out), .sel(or_9_out));  // open: in0
  Multiplexer #(.width(2), .disabled(0), .enable("false")) multiplexer_2 (
    .in1(2'b01), .out(multiplexer_1_out), .sel(or_4_out));  // open: in0
  Multiplexer #(.width(2), .disabled(0), .enable("false")) multiplexer_3 (
    .in1(2'b10), .out(multiplexer_1_out), .sel(or_5_out));  // open: in0
  Multiplexer #(.width(2), .disabled(0), .enable("false")) multiplexer_4 (
    .in1(2'b00), .out(multiplexer_4_out), .sel(or_10_out));  // open: in0
  Multiplexer #(.width(2), .disabled(0), .enable("false")) multiplexer_5 (
    .in1(2'b01), .out(multiplexer_4_out), .sel(or_6_out));  // open: in0
  Multiplexer #(.width(2), .disabled(0), .enable("false")) multiplexer_6 (
    .in1(2'b10), .out(multiplexer_4_out), .sel(MemW));  // open: in0
  Multiplexer #(.select(2), .width(2), .disabled(0), .enable("false")) multiplexer_7 (
    .in0(2'b00), .in1(2'b01), .in2(2'b10), .in3(2'b11), .out(ImmSrc), .sel(multiplexer_1_out));
  Multiplexer #(.select(2), .width(2), .disabled(0), .enable("false")) multiplexer_8 (
    .in0(2'b00), .in1(2'b01), .in2(2'b10), .in3(2'b11), .out(RegSrc), .sel(multiplexer_4_out));

  // Notes on the sheet:
  //   BL 24th bit
  //   Data Processing Exceptions that dont write result
endmodule

module decoder (
  input  [3:0] Rd,
  input  [1:0] OP,
  input  [5:0] Funct,
  output PCS,
  output RegW,
  output MemW,
  output MemtoReg,
  output ALUSrc,
  output [1:0] ImmSrc,
  output [1:0] RegSrc,
  output BL_indicate,
  output [1:0] ALUControl,
  output [1:0] FlagW,
  output MOV_indicate,
  output MVN_indicate
);

  wire alu_decoder_1_mov_indicate, alu_decoder_1_mvn_indicate, main_decoder_1_aluop, main_decoder_1_branch,
       not_1_out, not_2_out;

  main_decoder main_decoder_1 (
    .RegW(RegW), .MemW(MemW), .MemToReg(MemtoReg), .ALUSrc(ALUSrc), .ImmSrc(ImmSrc), .RegSrc(RegSrc),
    .Op(OP), .Branch(main_decoder_1_branch), .ALUOp(main_decoder_1_aluop), .in_1(Funct),
    .BL_indicate(BL_indicate));
  ALU_Decoder alu_decoder_1 (
    .in_2(Funct[4:0]), .ALUControl(ALUControl), .FlagW(FlagW), .ALUOp(main_decoder_1_aluop),
    .MOV_indicate(alu_decoder_1_mov_indicate), .MVN_indicate(alu_decoder_1_mvn_indicate));
  PC_Logic pc_logic_1 (.Rd(Rd), .PCS(PCS), .Branch(main_decoder_1_branch), .RegW(RegW));
  not not_1 (not_1_out, BL_indicate);
  and and_1 (MOV_indicate, not_1_out, alu_decoder_1_mov_indicate);
  not not_2 (not_2_out, BL_indicate);
  and and_2 (MVN_indicate, not_2_out, alu_decoder_1_mvn_indicate);

  // Notes on the sheet:
  //   PC Logic
  //   Main
  //   Decoder
  //   ALU
  //   Decoder
endmodule

module ALU_Decoder (
  input  ALUOp,
  input  [4:0] in_2,
  output [1:0] ALUControl,
  output [1:0] FlagW,
  output MOV_indicate,
  output MVN_indicate
);

  wire comparator_1_eq, comparator_2_eq, comparator_3_eq, comparator_4_eq, not_1_out;
  wire [1:0] multiplexer_1_out, multiplexer_2_out;

  // Probe on in_2
  not not_1 (not_1_out, ALUOp);
  Comparator #(.width(5)) comparator_1 (.a(in_2), .b(5'b11010), .eq(comparator_1_eq));  // open: gt, lt
  Comparator #(.width(5)) comparator_2 (.a(in_2), .b(5'b11011), .eq(comparator_2_eq));  // open: gt, lt
  Comparator #(.width(5)) comparator_3 (.a(in_2), .b(5'b11110), .eq(comparator_3_eq));  // open: gt, lt
  Comparator #(.width(5)) comparator_4 (.a(in_2), .b({5{1'b1}}), .eq(comparator_4_eq));  // open: gt, lt
  Multiplexer #(.select(5), .width(2), .disabled(0), .enable("false")) multiplexer_1 (
    .in0(2'b10), .in1(2'b10), .in4(2'b01), .in5(2'b01), .in8(2'b00), .in9(2'b00), .in20(2'b01), .in21(2'b01),
    .in24(2'b11), .in25(2'b11), .in26(2'b00), .in27(2'b00), .in30(2'b01), .in31(2'b01),
    .out(multiplexer_1_out), .sel(in_2));  // open: in2, in3, in6, in7, in10, in11, in12, in13, in14, in15, in16, in17, in18, in19, in22, in23, in28, in29
  Multiplexer #(.select(5), .width(2), .disabled(0), .enable("false")) multiplexer_2 (
    .in0(2'b00), .in1(2'b10), .in4(2'b00), .in5(2'b11), .in8(2'b00), .in9(2'b11), .in20(2'b00), .in21(2'b11),
    .in24(2'b00), .in25(2'b10), .in26(2'b00), .in27(2'b11), .in30(2'b00), .in31(2'b11),
    .out(multiplexer_2_out), .sel(in_2));  // open: in2, in3, in6, in7, in10, in11, in12, in13, in14, in15, in16, in17, in18, in19, in22, in23, in28, in29
  or or_1 (MOV_indicate, comparator_1_eq, comparator_3_eq, comparator_4_eq, comparator_2_eq);
  or or_2 (MVN_indicate, comparator_3_eq, comparator_4_eq);
  Multiplexer #(.width(2), .disabled(0), .enable("false")) multiplexer_3 (
    .in0(multiplexer_1_out), .in1(2'b00), .out(ALUControl), .sel(not_1_out));
  Multiplexer #(.width(2), .disabled(0), .enable("false")) multiplexer_4 (
    .in0(multiplexer_2_out), .in1(2'b00), .out(FlagW), .sel(not_1_out));

  // Notes on the sheet:
  //   AND
  //   SUB
  //   ADD
  //   CMP (SUB)
  //   ORR
  //   MOV (ADD)
  //   MVN (SUB)
  //   AND
  //   SUB
  //   ADD
  //   CMP (SUB)
  //   ORR
  //   MOV (ADD)
  //   MVN (SUB)
endmodule

module PC_Logic (
  input  [3:0] Rd,
  input  Branch,
  input  RegW,
  output PCS
);

  wire and_1_out, comparator_1_eq;

  Comparator #(.width(4)) comparator_1 (.a(Rd), .b(4'b1111), .eq(comparator_1_eq));  // open: gt, lt
  and and_1 (and_1_out, comparator_1_eq, RegW);
  or or_1 (PCS, and_1_out, Branch);
endmodule

module Conditional_Logic (
  input  CLK,
  input  PCS,
  input  RegW,
  input  MemW,
  input  [1:0] FlagW,
  input  [3:0] Cond,
  input  [3:0] ALUFlags,
  input  CLR,
  output PCSrc,
  output RegWrite,
  output MemWrite
);

  wire condition_check_1_cond_ex;
  wire [1:0] and_1_out, bit_extender_1_out, register_1_q, register_2_q;

  Register #(.width(2)) register_1 (.D(ALUFlags[3:2]), .en(and_1_out[1]), .Q(register_1_q), .clk(CLK), .clr(CLR));
  Register #(.width(2)) register_2 (.D(ALUFlags[1:0]), .en(and_1_out[0]), .Q(register_2_q), .clk(CLK), .clr(CLR));
  assign and_1_out = FlagW & bit_extender_1_out;  // AND_Gate and_1, 2 bits wide
  Condition_Check condition_check_1 (
    .Cond(Cond), .NZ(register_1_q), .CV(register_2_q), .Cond_Ex(condition_check_1_cond_ex));
  and and_2 (PCSrc, PCS, condition_check_1_cond_ex);
  and and_3 (RegWrite, RegW, condition_check_1_cond_ex);
  and and_4 (MemWrite, MemW, condition_check_1_cond_ex);
  assign bit_extender_1_out = {{1{condition_check_1_cond_ex}}, condition_check_1_cond_ex};  // Bit_Extender bit_extender_1
endmodule

// 1
module Condition_Check (
  input  [3:0] Cond,
  input  [1:0] NZ,
  input  [1:0] CV,
  output Cond_Ex
);

  wire AL_out, and_1_out, comparator_1_eq, EQ_out, GT_out, not_1_out, not_2_out, not_3_out, not_4_out,
       not_5_out, not_6_out, not_7_out, not_8_out;

  not not_1 (not_1_out, Cond[0]);
  not not_2 (not_2_out, Cond[0]);
  not not_3 (not_3_out, Cond[1]);
  not not_4 (not_4_out, Cond[2]);
  not not_5 (not_5_out, Cond[3]);
  not not_6 (not_6_out, Cond[0]);
  not not_7 (not_7_out, Cond[1]);
  not not_8 (not_8_out, NZ[0]);
  and AL (AL_out, not_1_out, Cond[1], Cond[2], Cond[3]);
  and EQ (EQ_out, not_2_out, not_3_out, not_4_out, not_5_out, NZ[0]);
  and GT (GT_out, not_6_out, not_7_out, Cond[2], Cond[3], not_8_out);
  Comparator #(.width(1)) comparator_1 (.a(NZ[1]), .b(CV[0]), .eq(comparator_1_eq));  // open: gt, lt
  and and_1 (and_1_out, GT_out, comparator_1_eq);
  or or_1 (Cond_Ex, AL_out, EQ_out, and_1_out);
endmodule

module Control_Unit (
  input  CLK,
  input  [3:0] Cond,
  input  [3:0] ALUFlags,
  input  [1:0] Op,
  input  [5:0] Funct,
  input  [3:0] Rd,
  input  CLR,
  output PCSrc,
  output RegWrite,
  output MemWrite,
  output MemtoReg,
  output ALUSrc,
  output [1:0] ImmSrc,
  output [1:0] RegSrc,
  output MVN_indicate,
  output BL_indicate,
  output [1:0] ALUControl,
  output MOV_indicate
);

  wire decoder_1_memw, decoder_1_pcs, decoder_1_regw;
  wire [1:0] decoder_1_flagw;

  decoder decoder_1 (
    .Rd(Rd), .OP(Op), .Funct(Funct), .PCS(decoder_1_pcs), .RegW(decoder_1_regw), .MemW(decoder_1_memw),
    .MemtoReg(MemtoReg), .ALUSrc(ALUSrc), .ImmSrc(ImmSrc), .RegSrc(RegSrc), .ALUControl(ALUControl),
    .FlagW(decoder_1_flagw), .MOV_indicate(MOV_indicate), .BL_indicate(BL_indicate),
    .MVN_indicate(MVN_indicate));
  Conditional_Logic conditional_logic_1 (
    .PCS(decoder_1_pcs), .RegW(decoder_1_regw), .MemW(decoder_1_memw), .FlagW(decoder_1_flagw), .Cond(Cond),
    .ALUFlags(ALUFlags), .PCSrc(PCSrc), .RegWrite(RegWrite), .MemWrite(MemWrite), .CLK(CLK), .CLR(CLR));
endmodule
